// Digital circuit InstructionDecoder.dig as structural Verilog
// The InstructionDecoder component, which serves as a hub to control many of the signals to other components. It implements both the fetch operation, and execution of machine code (including decoding).
module InstructionDecoder (
  input  [31:0] Instruction,
  input  Fetch,
  input  Execute,
  output [3:0] Reg_dest,
  output [3:0] Reg_B,
  output [3:0] Reg_A,
  output [2:0] Opcode,
  output [3:0] Condition,
  output nRE,
  output nWE,
  output Constant,
  output SetFlags
);

  Multiplexer #(.Bits(3)) multiplexer_1 (.sel(Instruction[31]), .in_0(Instruction[30:28]), .in_1(3'b000), .out(Opcode));
  Multiplexer multiplexer_2 (.sel(Instruction[26]), .in_0(Instruction[16]), .in_1(1'b0), .out(Constant));
  Multiplexer multiplexer_3 (.sel(Instruction[26]), .in_0(1'b0), .in_1(Instruction[12]), .out(Reg_A[0]));
  // Pins of 1 and 4 bits meet at Reg_A
  // Pins of 1 and 10 bits meet at Instruction[25:16]
  // Pins of 1 and 10 bits meet at {10{1'b0}}
  // Pins of 1 and 4 bits meet at Instruction[15:12]
  // Pins of 1 and 4 bits meet at 4'b0000

  assign Condition = Instruction[3:0];
  assign Reg_B = Instruction[11:8];
  assign Reg_dest = Instruction[7:4];
  assign SetFlags = Instruction[27];

  // Notes on the sheet:
  //   Instruction: The instruction machine code input. If the CPU is in the fetch phase and a rising clock signal occurs, this machine code is stored in the internal instruction register (IR), so that it can be decoded and executed.
  //   Reg_dest: Destination register output, which determines the register that should store the result of a data operation. A data operation is either an ALU computation, or a read from an external device, such as RAM.
  //   Reg_B: B register output, which determines the register to be used for the second operand.
  //   Reg_A: A register output, which determines the register to be used for the first operand.
  //   Opcode: Opcode output, which determines the operation the ALU should perform.
  //   Condition: Instruction condition output, which contains the condition under which the instruction should be executed.
endmodule
